# Fritzing sketch 20200223_slimeCV_Flash_slime_lapse_wiring (saved by Fritzing 0.9.3b)
breadboards: 1

parts:
  Raspberry_Pi_1 = Raspberry Pi 3 [part_number=RPI-3-V1.2]
  LED1 = LED - 5mm [color="White (6500K)" package="5 mm [THT]"]
  LED2 = smd LED [color="White (6500K)" package="0603 [SMD]"]
  R1 = Resistor [tolerance=±5% resistance=1k package=THT]
  R2 = Resistor [tolerance=±5% resistance=220 package=THT]

nets:
  N1: Raspberry_Pi_1.GPIO15, LED2.anode
  N2: Raspberry_Pi_1.GPIO14, LED1.anode
  N3: Raspberry_Pi_1.GND, R1.Pin_0, R2.Pin_0
  N4: LED1.cathode, R1.Pin_1
  N5: LED2.cathode, R2.Pin_1

notes:
  N.B. resistor values might not be the same depending on desired lighting intensity. Requires trial and error.
